# Fritzing sketch circuit_scheme (saved by Fritzing 0.9.3b)
breadboards: 6

parts:
  Part1 = Arduino Uno (Rev3)
  U1 = 74HC595 [package="DIP16 [THT]"]
  U2 = 74HC595 [package="DIP16 [THT]"]
  U3 = 74HC595 [package="DIP16 [THT]"]
  U4 = 74HC595 [package="DIP16 [THT]"]
  IC1 = DS1307 [package=THT]
  R1 = Resistor [tolerance=±5% resistance=220 package=THT]
  R2 = Resistor [tolerance=±5% resistance=220 package=THT]
  R3 = Resistor [tolerance=±5% resistance=220 package=THT]
  R4 = Resistor [tolerance=±5% resistance=220 package=THT]
  R5 = Resistor [tolerance=±5% resistance=220 package=THT]
  R6 = Resistor [tolerance=±5% resistance=220 package=THT]
  R7 = Resistor [tolerance=±5% resistance=220 package=THT]
  R8 = Resistor [tolerance=±5% resistance=220 package=THT]
  LED1 = LED - 3mm [color="Red (633nm)" package="3 mm [THT]"]
  LED2 = LED - 3mm [color="Red (633nm)" package="3 mm [THT]"]
  LED3 = LED - 3mm [color="Red (633nm)" package="3 mm [THT]"]
  LED4 = LED - 3mm [color="Red (633nm)" package="3 mm [THT]"]
  LED5 = LED - 3mm [color="Red (633nm)" package="3 mm [THT]"]
  LED6 = LED - 3mm [color="Red (633nm)" package="3 mm [THT]"]
  LED7 = LED - 3mm [color="Red (633nm)" package="3 mm [THT]"]
  LED8 = LED - 3mm [color="Red (633nm)" package="3 mm [THT]"]
  R9 = Resistor [tolerance=±5% resistance=220 package=THT]
  R10 = Resistor [tolerance=±5% resistance=220 package=THT]
  R11 = Resistor [tolerance=±5% resistance=220 package=THT]
  R12 = Resistor [tolerance=±5% resistance=220 package=THT]
  R13 = Resistor [tolerance=±5% resistance=220 package=THT]
  R14 = Resistor [tolerance=±5% resistance=220 package=THT]
  R15 = Resistor [tolerance=±5% resistance=220 package=THT]
  R16 = Resistor [tolerance=±5% resistance=220 package=THT]
  LED9 = LED - 3mm [color="Red (633nm)" package="3 mm [THT]"]
  LED10 = LED - 3mm [color="Red (633nm)" package="3 mm [THT]"]
  LED11 = LED - 3mm [color="Red (633nm)" package="3 mm [THT]"]
  LED12 = LED - 3mm [color="Red (633nm)" package="3 mm [THT]"]
  LED13 = LED - 3mm [color="Red (633nm)" package="3 mm [THT]"]
  LED14 = LED - 3mm [color="Red (633nm)" package="3 mm [THT]"]
  LED15 = LED - 3mm [color="Red (633nm)" package="3 mm [THT]"]
  LED16 = LED - 3mm [color="Red (633nm)" package="3 mm [THT]"]
  R17 = Resistor [tolerance=±5% resistance=220 package=THT]
  R18 = Resistor [tolerance=±5% resistance=220 package=THT]
  R19 = Resistor [tolerance=±5% resistance=220 package=THT]
  R20 = Resistor [tolerance=±5% resistance=220 package=THT]
  R21 = Resistor [tolerance=±5% resistance=220 package=THT]
  R22 = Resistor [tolerance=±5% resistance=220 package=THT]
  R23 = Resistor [tolerance=±5% resistance=220 package=THT]
  R24 = Resistor [tolerance=±5% resistance=220 package=THT]
  LED17 = LED - 3mm [color="Red (633nm)" package="3 mm [THT]"]
  LED18 = LED - 3mm [color="Red (633nm)" package="3 mm [THT]"]
  LED19 = LED - 3mm [color="Red (633nm)" package="3 mm [THT]"]
  LED20 = LED - 3mm [color="Red (633nm)" package="3 mm [THT]"]
  LED21 = LED - 3mm [color="Red (633nm)" package="3 mm [THT]"]
  LED22 = LED - 3mm [color="Red (633nm)" package="3 mm [THT]"]
  LED23 = LED - 3mm [color="Red (633nm)" package="3 mm [THT]"]
  LED24 = LED - 3mm [color="Red (633nm)" package="3 mm [THT]"]
  R25 = Resistor [tolerance=±5% resistance=220 package=THT]
  R26 = Resistor [tolerance=±5% resistance=220 package=THT]
  R27 = Resistor [tolerance=±5% resistance=220 package=THT]
  R28 = Resistor [tolerance=±5% resistance=220 package=THT]
  R29 = Resistor [tolerance=±5% resistance=220 package=THT]
  R30 = Resistor [tolerance=±5% resistance=220 package=THT]
  R31 = Resistor [tolerance=±5% resistance=220 package=THT]
  LED25 = LED - 3mm [color="Red (633nm)" package="3 mm [THT]"]
  LED26 = LED - 3mm [color="Red (633nm)" package="3 mm [THT]"]
  LED27 = LED - 3mm [color="Red (633nm)" package="3 mm [THT]"]
  LED28 = LED - 3mm [color="Red (633nm)" package="3 mm [THT]"]
  LED29 = LED - 3mm [color="Red (633nm)" package="3 mm [THT]"]
  LED30 = LED - 3mm [color="Red (633nm)" package="3 mm [THT]"]
  LED31 = LED - 3mm [color="Red (633nm)" package="3 mm [THT]"]

nets:
  N1: Part1.A4/SDA, IC1.SDA_-_I2C_Data
  N2: Part1.A5/SCL, IC1.SCL_-_I2C_Clock
  N3: Part1.D8, U1.ST_CP, U2.ST_CP, U3.ST_CP, U4.ST_CP
  N4: Part1.D11_PWM/MOSI, U1.DS
  N5: Part1.D12/MISO, U1.SH_CP, U2.SH_CP, U3.SH_CP, U4.SH_CP
  GND: Part1.GND, U1.GND, U1.OE, U2.GND, U2.OE, U3.GND, U3.OE, U4.GND, U4.OE, IC1.0V, LED1.anode, LED2.anode, LED3.anode, LED4.anode, LED5.anode, LED6.anode, LED7.anode, LED8.anode, LED9.anode, LED10.anode, LED11.anode, LED12.anode, LED13.anode, LED14.anode, LED15.anode, LED16.anode, LED17.anode, LED18.anode, LED19.anode, LED20.anode, LED21.anode, LED22.anode, LED23.anode, LED24.anode, LED25.anode, LED26.anode, LED27.anode, LED28.anode, LED29.anode, LED30.anode, LED31.anode
  VCC: Part1.5V, U1.MR, U1.VCC, U2.MR, U2.VCC, U3.MR, U3.VCC, U4.MR, U4.VCC, IC1.+V
  N6: U1.Q1, R2.Pin_0
  N7: U1.Q2, R3.Pin_0
  N8: U1.Q3, R4.Pin_0
  N9: U1.Q4, R5.Pin_0
  N10: U1.Q5, R6.Pin_0
  N11: U1.Q6, R7.Pin_0
  N12: U1.Q7, R8.Pin_0
  N13: U1.Q7', U2.DS
  N14: U1.Q0, R1.Pin_0
  N15: U2.Q1, R10.Pin_0
  N16: U2.Q2, R11.Pin_0
  N17: U2.Q3, R12.Pin_0
  N18: U2.Q4, R13.Pin_0
  N19: U2.Q5, R14.Pin_0
  N20: U2.Q6, R15.Pin_0
  N21: U2.Q7, R16.Pin_0
  N22: U2.Q7', U3.DS
  N23: U2.Q0, R9.Pin_0
  N24: U3.Q1, R18.Pin_0
  N25: U3.Q2, R19.Pin_0
  N26: U3.Q3, R20.Pin_0
  N27: U3.Q4, R21.Pin_0
  N28: U3.Q5, R22.Pin_0
  N29: U3.Q6, R23.Pin_0
  N30: U3.Q7, R24.Pin_0
  N31: U3.Q7', U4.DS
  N32: U3.Q0, R17.Pin_0
  N33: U4.Q1, R26.Pin_0
  N34: U4.Q2, R27.Pin_0
  N35: U4.Q3, R28.Pin_0
  N36: U4.Q4, R29.Pin_0
  N37: U4.Q5, R30.Pin_0
  N38: U4.Q6, R31.Pin_0
  N39: U4.Q0, R25.Pin_0
  N40: R1.Pin_1, LED1.cathode
  N41: R2.Pin_1, LED2.cathode
  N42: R3.Pin_1, LED3.cathode
  N43: R4.Pin_1, LED4.cathode
  N44: R5.Pin_1, LED5.cathode
  N45: R6.Pin_1, LED6.cathode
  N46: R7.Pin_1, LED7.cathode
  N47: R8.Pin_1, LED8.cathode
  N48: R9.Pin_1, LED9.cathode
  N49: R10.Pin_1, LED10.cathode
  N50: R11.Pin_1, LED11.cathode
  N51: R12.Pin_1, LED12.cathode
  N52: R13.Pin_1, LED13.cathode
  N53: R14.Pin_1, LED14.cathode
  N54: R15.Pin_1, LED15.cathode
  N55: R16.Pin_1, LED16.cathode
  N56: R17.Pin_1, LED17.cathode
  N57: R18.Pin_1, LED18.cathode
  N58: R19.Pin_1, LED19.cathode
  N59: R20.Pin_1, LED20.cathode
  N60: R21.Pin_1, LED21.cathode
  N61: R22.Pin_1, LED22.cathode
  N62: R23.Pin_1, LED23.cathode
  N63: R24.Pin_1, LED24.cathode
  N64: R25.Pin_1, LED25.cathode
  N65: R26.Pin_1, LED26.cathode
  N66: R27.Pin_1, LED27.cathode
  N67: R28.Pin_1, LED28.cathode
  N68: R29.Pin_1, LED29.cathode
  N69: R30.Pin_1, LED30.cathode
  N70: R31.Pin_1, LED31.cathode

notes:
  Note 1: The actual RTC element used was DS1338. It was wired the same way - same pins on the element connected to the same pins on the Arduino
  Note 2: Real project used 1 breadboard for all shift registeres, and 2 breadboards for LEDs
